# Fritzing sketch FritzingSketch (saved by Fritzing 0.9.3b)
breadboards: 1

parts:
  Power_plug1 = Power plug
  Часть2 = Arduino Nano (Rev3.0)
  Nokia_5110_LCD_Module1 = Nokia 5110 LCD
  AM1 = AM2320 Humidity and Temperature Sensor [part_number="Adafruit #3721"]
  Часть3 = Adafruit DS3231 [part_number="Adafruit #3013"]
  SD_card_module1 = SD Card Module
  R1 = Resistor [tolerance=±5% resistance=5k package="1206 [SMD]"]
  R2 = Resistor [tolerance=±5% resistance=20k package="1206 [SMD]"]

nets:
  GND: Power_plug1.GND, Часть2.GND, Часть2.D2, Часть2.D3, Часть2.RESET, Nokia_5110_LCD_Module1.LED, Nokia_5110_LCD_Module1.LED_(out), AM1.SDA, Часть3.GND, SD_card_module1.GND#0, SD_card_module1.+3.3, R2.Pin_0
  VIN: Power_plug1.VCC, Часть2.VIN, Nokia_5110_LCD_Module1.DN(MOSI), Nokia_5110_LCD_Module1.SCLK, Nokia_5110_LCD_Module1.DN(MODI)_(out), AM1.VDD, Часть3.Vin, SD_card_module1.+5, R2.Pin_1
  N1: Часть2.D4, Nokia_5110_LCD_Module1.GND
  N2: Часть2.D5, Nokia_5110_LCD_Module1.SCE
  N3: Часть2.D6, Часть2.D7, Nokia_5110_LCD_Module1.VCC
  N4: Часть2.D9, Часть2.D10, SD_card_module1.CS
  N5: Часть2.D11/MOSI, Nokia_5110_LCD_Module1.RST, SD_card_module1.MOSI
  N6: Часть2.D12/MISO, SD_card_module1.MISO, SD_card_module1.GND#7
  N7: Часть2.A6, Часть2.A5, Часть3.SCL
  N8: Часть2.A4, Часть2.A3, Часть3.SDA, Часть3.BAT
  N9: Часть2.3V3, Часть2.D13/SCK, Nokia_5110_LCD_Module1.D/C, SD_card_module1.SCK
  N10: AM1.GND, R1.Pin_0
  N11: AM1.SCL, R1.Pin_1

notes:
  Ground
  +5V
  330
  DS3231 RTC
  AM2320
  8544 Nokia LCD
  SD card
  5K
  20K

custom parts:
  Nokia 5110 LCD: Nokia 5110 Graphic 84*48 LCD module such as the Sparkfun LCD-10168 or the clones from Ebay. There is example code for the Arduino available from the Sparkfun site in https://learn.sparkfun.com/tutorials/graphic-lcd-hookup-guide This is a 3.3V device, if you are running it from a 5V micro you need a 5V tolorant level translator such as the 74ahc367 to protect the signal imputs. Rafa G. did a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
  AM2320 Humidity and Temperature Sensor: AM2320 I2C Humidity and Temperature Sensor
  Adafruit DS3231: The datasheet for the DS3231 explains that this part is an "Extremely Accurate I²C-Integrated RTC/TCXO/Crystal". And, hey, it does exactly what it says on the tin! This Real Time Clock (RTC) is the most precise you can get in a small, low power package. Most RTCs use an external 32kHz timing crystal that is used to keep time with low current draw. And that's all well and good, but those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
  SD Card Module: SD Card Module Slot Socket Reader For Arduino ARM MCU
